# Fritzing sketch currentsource_mod (saved by Fritzing 0.9.2b)
circuit board: 2cm x 3.5cm
breadboards: 1

parts:
  OPAMP1 = Dual Op-Amp [package=dip08]
  NCHANpwr = Basic FET N-Channel [package="TO220 [THT]"]
  I_out- = Header 1 [package=1x01_offset]
  I_out+ = Header 1 [package=1x01_offset]
  V_pwr+ = Header 1 [package=1x01_offset]
  GND_pwr = Header 1 [package=1x01_offset]
  Cisetfilter = Electrolytic Capacitor [capacitance=1µF package="100 mil [THT, electrolytic]"]
  I_set = Header 1 [package=1x01_offset]
  V_ctl = Header 1 [package=1x01_offset]
  GND_ctrl = Header 1 [package=1x01_offset]
  PWM = Header 1 [package=1x01_offset]
  Rpwm2 = Resistor [tolerance=±5% resistance=100k power=2W package="1206 [SMD]"]
  Rsense = Resistor [tolerance=±5% resistance=0.1 power=2W package="2010 [SMD]"]
  Risetfilter = Resistor [tolerance=±5% resistance=100k package="1206 [SMD]"]
  R3 = Resistor [tolerance=±5% resistance=100k package="1206 [SMD]"]
  Rmosfet1 = Resistor [tolerance=±5% resistance=100 package="1206 [SMD]"]
  Rpwm1 = Resistor [tolerance=±5% resistance=1k package="1206 [SMD]"]
  NPNpwm = PNP-Transistor [package="TO92 [THT]"]

nets (from the schematic view):
  N1: OPAMP1.A_OUT, OPAMP1.A_-IN, R3.Pin_0
  N2: OPAMP1.A_+IN, Cisetfilter.+, Risetfilter.Pin_1
  N3: OPAMP1.A_V-, GND_pwr.1, Cisetfilter.-, GND_ctrl.1, Rpwm2.Pin_1, Rsense.Pin_1, NPNpwm.E
  N4: OPAMP1.B_+IN, R3.Pin_1, NPNpwm.C
  N5: OPAMP1.B_-IN, NCHANpwr.source, Rsense.Pin_0
  N6: OPAMP1.B_OUT, Rmosfet1.Pin_0
  N7: OPAMP1.A_V+, V_ctl.1
  N8: NCHANpwr.gate, Rmosfet1.Pin_1
  N9: NCHANpwr.drain, I_out-.1
  N10: I_out+.1, V_pwr+.1
  N11: I_set.1, Risetfilter.Pin_0
  N12: PWM.1, Rpwm2.Pin_0, Rpwm1.Pin_0
  N13: Rpwm1.Pin_1, NPNpwm.B
